// Logisim project CPU.circ as structural Verilog: 11 circuits, main circuit main
module main (
  input  reset,
  input  RAMreset
);

  wire clk, KBRE, keyboard_1_avail, multiplexer_6_out, MUX_0_jal, MUX_ALUResult_Memory, MUX_Rd_Rt,
       MUX_RtData_Imm, not_2_out, RAMWE, RegWE, TTYWE;
  wire [1:0] MUX_nobranch_beq_blt, MUX_nojump_jjal_jr, \or ;
  wire [2:0] ALUop, multiplexer_3_out, multiplexer_4_out, Rd, Rs, Rt, ShAmt;
  wire [3:0] UpperFourBits;
  wire [5:0] Immed;
  wire [6:0] keyboard_1_data;
  wire [7:0] KBData;
  wire [11:0] Addr, programcounter_1_output;
  wire [15:0] alu_1_outputdata, alu_2_outputdata, alu_3_outputdata, multiplexer_1_out, multiplexer_2_out,
       multiplexer_7_out, multiplexer_8_out, multiplexer_9_out, multiplexer_10_out, ram_1_data,
       registerfile_1_readdata2, rom_1_data, RsData, signextender_1_out_2;

  // Probe on RsData[6:0]
  TTY #(.rows(13), .cols(80), .trigger("falling")) tty_1 (.data(RsData[6:0]), .clk(clk), .we(TTYWE), .clr(reset));
  ProgramCounter programcounter_1 (
    .Clock(clk), .reset(reset), .Output({UpperFourBits, programcounter_1_output}), .Input(multiplexer_9_out));
  Clock u_clk (.out(clk));
  // Probe on multiplexer_9_out
  ALU alu_1 (
    .ALUOp(3'b000), .InputData1({UpperFourBits, programcounter_1_output}), .InputData2(16'h1),
    .OutputData(alu_1_outputdata));  // open: ShiftAmt, Relation
  ROM #(.addrWidth(16), .dataWidth(16)) rom_1 (
    .addr({UpperFourBits, programcounter_1_output}), .data(rom_1_data));  // open: sel
  // Probe on rom_1_data
  InstructionDecoder instructiondecoder_1 (
    .ManualInstruction(rom_1_data), .Rs(Rs), .Rt(Rt), .Rd(Rd), .ShAmt(ShAmt), .Imm(Immed), .Addr(Addr),
    .RegWriteEnable(RegWE), .RAMWriteEnable(RAMWE), .MUX_RtData_Imm(MUX_RtData_Imm), .MUX_Rd_Rt(MUX_Rd_Rt),
    .MUX_ALU_Result_Memory(MUX_ALUResult_Memory), .ALUOpType(ALUop), .MUX_0_beq_blt(MUX_nobranch_beq_blt),
    .MUX_0_j_jr(MUX_nojump_jjal_jr), .MUX_0_jal(MUX_0_jal), .TTYWriteEnable(TTYWE), .KeyboardRE(KBRE));
  Keyboard keyboard_1 (.clk(clk), .re(KBRE), .clr(reset), .avail(keyboard_1_avail), .data(keyboard_1_data));
  Multiplexer #(.width(16), .enable("false")) multiplexer_1 (
    .in0(multiplexer_10_out), .in1(alu_1_outputdata), .out(multiplexer_1_out), .sel(MUX_0_jal));
  Multiplexer #(.width(16), .enable("false")) multiplexer_2 (
    .in0(multiplexer_1_out), .in1({{8{1'b0}}, KBData}), .out(multiplexer_2_out), .sel(KBRE));
  Multiplexer #(.width(3), .enable("false")) multiplexer_3 (
    .in0(multiplexer_4_out), .in1(3'b111), .out(multiplexer_3_out), .sel(MUX_0_jal));
  // Probe on multiplexer_4_out
  Multiplexer #(.width(3), .enable("false")) multiplexer_4 (
    .in0(Rd), .in1(Rt), .out(multiplexer_4_out), .sel(MUX_Rd_Rt));
  Multiplexer #(.width(7), .enable("false")) multiplexer_5 (
    .in0(keyboard_1_data), .in1({7{1'b0}}), .out(KBData[6:0]), .sel(KBData[7]));
  not not_1 (KBData[7], keyboard_1_avail);
  Multiplexer #(.select(2), .enable("false")) multiplexer_6 (
    .in0(1'b0), .in1(\or [1]), .in2(\or [0]), .out(multiplexer_6_out), .sel(MUX_nobranch_beq_blt));  // open: in3
  // Probe on Rs
  // Probe on {{8{1'b0}}, KBData}
  // Probe on multiplexer_10_out
  RegisterFile registerfile_1 (
    .WriteRegister(multiplexer_3_out), .WriteData(multiplexer_2_out), .reset(reset),
    .RegisterWriteEnable(RegWE), .ReadRegister1(Rs), .ReadRegister2(Rt), .Clock(clk), .ReadData1(RsData),
    .ReadData2(registerfile_1_readdata2));
  // Probe on Rt
  // Probe on RsData
  Multiplexer #(.width(16), .enable("false")) multiplexer_7 (
    .in0(registerfile_1_readdata2), .in1(signextender_1_out_2), .out(multiplexer_7_out), .sel(MUX_RtData_Imm));
  // Probe on signextender_1_out_2
  SignExtender signextender_1 (.in_1(Immed), .out_2(signextender_1_out_2));
  ALU alu_2 (
    .ALUOp(3'b000), .InputData1(alu_1_outputdata), .InputData2(signextender_1_out_2),
    .OutputData(alu_2_outputdata));  // open: ShiftAmt, Relation
  // Probe on multiplexer_7_out
  ALU alu_3 (
    .ALUOp(ALUop), .InputData1(RsData), .InputData2(multiplexer_7_out), .OutputData(alu_3_outputdata),
    .ShiftAmt(ShAmt), .Relation(\or ));
  Multiplexer #(.width(16), .enable("false")) multiplexer_8 (
    .in0(alu_1_outputdata), .in1(alu_2_outputdata), .out(multiplexer_8_out), .sel(multiplexer_6_out));
  not not_2 (not_2_out, clk);
  Multiplexer #(.select(2), .width(16), .enable("false")) multiplexer_9 (
    .in0(multiplexer_8_out), .in1({UpperFourBits, Addr}), .in2(RsData), .out(multiplexer_9_out),
    .sel(MUX_nojump_jjal_jr));  // open: in3
  RAM #(.addrWidth(16), .dataWidth(16), .bus("separate")) ram_1 (
    .addr(alu_3_outputdata), .din(registerfile_1_readdata2), .data(ram_1_data), .str(RAMWE), .clk(not_2_out),
    .clr(RAMreset));  // open: sel, ld
  Multiplexer #(.width(16), .enable("false")) multiplexer_10 (
    .in0(alu_3_outputdata), .in1(ram_1_data), .out(multiplexer_10_out), .sel(MUX_ALUResult_Memory));

  // Notes on the sheet:
  //   Instruction Memory
  //   contents of rom_1 (hex, n*v repeats v):
  //   0 f008 62a0 e400
  //   input1 < input2
  //   equal
  //   Data Memory
endmodule

module Register (
  input  Clock,
  input  WriteEnable,
  input  reset,
  input  [15:0] Input,
  output [15:0] Output
);

  D_Flip_Flop #(.trigger("falling")) d_ff_1 (
    .clk(Clock), .D(Input[0]), .Q(Output[0]), .en(WriteEnable), .reset(reset));  // open: Qn, preset
  D_Flip_Flop #(.trigger("falling")) d_ff_2 (
    .clk(Clock), .D(Input[1]), .Q(Output[1]), .en(WriteEnable), .reset(reset));  // open: Qn, preset
  D_Flip_Flop #(.trigger("falling")) d_ff_3 (
    .clk(Clock), .D(Input[2]), .Q(Output[2]), .en(WriteEnable), .reset(reset));  // open: Qn, preset
  D_Flip_Flop #(.trigger("falling")) d_ff_4 (
    .clk(Clock), .D(Input[3]), .Q(Output[3]), .en(WriteEnable), .reset(reset));  // open: Qn, preset
  D_Flip_Flop #(.trigger("falling")) d_ff_5 (
    .clk(Clock), .D(Input[4]), .Q(Output[4]), .en(WriteEnable), .reset(reset));  // open: Qn, preset
  D_Flip_Flop #(.trigger("falling")) d_ff_6 (
    .clk(Clock), .D(Input[5]), .Q(Output[5]), .en(WriteEnable), .reset(reset));  // open: Qn, preset
  D_Flip_Flop #(.trigger("falling")) d_ff_7 (
    .clk(Clock), .D(Input[6]), .Q(Output[6]), .en(WriteEnable), .reset(reset));  // open: Qn, preset
  D_Flip_Flop #(.trigger("falling")) d_ff_8 (
    .clk(Clock), .D(Input[7]), .Q(Output[7]), .en(WriteEnable), .reset(reset));  // open: Qn, preset
  D_Flip_Flop #(.trigger("falling")) d_ff_9 (
    .clk(Clock), .D(Input[8]), .Q(Output[8]), .en(WriteEnable), .reset(reset));  // open: Qn, preset
  D_Flip_Flop #(.trigger("falling")) d_ff_10 (
    .clk(Clock), .D(Input[9]), .Q(Output[9]), .en(WriteEnable), .reset(reset));  // open: Qn, preset
  D_Flip_Flop #(.trigger("falling")) d_ff_11 (
    .clk(Clock), .D(Input[10]), .Q(Output[10]), .en(WriteEnable), .reset(reset));  // open: Qn, preset
  D_Flip_Flop #(.trigger("falling")) d_ff_12 (
    .clk(Clock), .D(Input[11]), .Q(Output[11]), .en(WriteEnable), .reset(reset));  // open: Qn, preset
  D_Flip_Flop #(.trigger("falling")) d_ff_13 (
    .clk(Clock), .D(Input[12]), .Q(Output[12]), .en(WriteEnable), .reset(reset));  // open: Qn, preset
  D_Flip_Flop #(.trigger("falling")) d_ff_14 (
    .clk(Clock), .D(Input[13]), .Q(Output[13]), .en(WriteEnable), .reset(reset));  // open: Qn, preset
  D_Flip_Flop #(.trigger("falling")) d_ff_15 (
    .clk(Clock), .D(Input[14]), .Q(Output[14]), .en(WriteEnable), .reset(reset));  // open: Qn, preset
  D_Flip_Flop #(.trigger("falling")) d_ff_16 (
    .clk(Clock), .D(Input[15]), .Q(Output[15]), .en(WriteEnable), .reset(reset));  // open: Qn, preset

  // Other names for the same wires on the sheet: clk = Clock; WE = WriteEnable
endmodule

module RegisterFile (
  input  [2:0] WriteRegister,
  input  [15:0] WriteData,
  input  reset,
  input  RegisterWriteEnable,
  input  [2:0] ReadRegister1,
  input  [2:0] ReadRegister2,
  input  Clock,
  output [15:0] ReadData1,
  output [15:0] ReadData2
);

  wire and_1_out, and_2_out, and_3_out, and_4_out, and_5_out, and_6_out, and_7_out, decoder_1_out1,
       decoder_1_out2, decoder_1_out3, decoder_1_out4, decoder_1_out5, decoder_1_out6, decoder_1_out7;
  wire [15:0] register_1_output, register_2_output, register_3_output, register_4_output, register_5_output,
       register_6_output, register_7_output, register_8_output;

  Decoder #(.select(3)) decoder_1 (
    .out1(decoder_1_out1), .out2(decoder_1_out2), .out3(decoder_1_out3), .out4(decoder_1_out4),
    .out5(decoder_1_out5), .out6(decoder_1_out6), .out7(decoder_1_out7), .sel(WriteRegister));  // open: out0, en
  Register register_1 (.Clock(Clock), .WriteEnable(1'b0), .reset(reset), .Input(WriteData), .Output(register_1_output));
  Register register_2 (
    .Clock(Clock), .WriteEnable(and_1_out), .reset(reset), .Input(WriteData), .Output(register_2_output));
  and and_1 (and_1_out, decoder_1_out1, RegisterWriteEnable);
  Register register_3 (
    .Clock(Clock), .WriteEnable(and_2_out), .reset(reset), .Input(WriteData), .Output(register_3_output));
  and and_2 (and_2_out, decoder_1_out2, RegisterWriteEnable);
  Register register_4 (
    .Clock(Clock), .WriteEnable(and_3_out), .reset(reset), .Input(WriteData), .Output(register_4_output));
  and and_3 (and_3_out, decoder_1_out3, RegisterWriteEnable);
  Register register_5 (
    .Clock(Clock), .WriteEnable(and_4_out), .reset(reset), .Input(WriteData), .Output(register_5_output));
  and and_4 (and_4_out, decoder_1_out4, RegisterWriteEnable);
  Register register_6 (
    .Clock(Clock), .WriteEnable(and_5_out), .reset(reset), .Input(WriteData), .Output(register_6_output));
  and and_5 (and_5_out, decoder_1_out5, RegisterWriteEnable);
  Register register_7 (
    .Clock(Clock), .WriteEnable(and_6_out), .reset(reset), .Input(WriteData), .Output(register_7_output));
  and and_6 (and_6_out, decoder_1_out6, RegisterWriteEnable);
  Register register_8 (
    .Clock(Clock), .WriteEnable(and_7_out), .reset(reset), .Input(WriteData), .Output(register_8_output));
  and and_7 (and_7_out, decoder_1_out7, RegisterWriteEnable);
  // Probe on register_1_output
  // Probe on register_2_output
  // Probe on register_3_output
  // Probe on register_4_output
  // Probe on register_5_output
  // Probe on register_6_output
  // Probe on register_7_output
  // Probe on register_8_output
  Multiplexer #(.select(3), .width(16)) multiplexer_1 (
    .in0(register_1_output), .in1(register_2_output), .in2(register_3_output), .in3(register_4_output),
    .in4(register_5_output), .in5(register_6_output), .in6(register_7_output), .in7(register_8_output),
    .out(ReadData1), .sel(ReadRegister1));  // open: en
  Multiplexer #(.select(3), .width(16)) multiplexer_2 (
    .in0(register_1_output), .in1(register_2_output), .in2(register_3_output), .in3(register_4_output),
    .in4(register_5_output), .in5(register_6_output), .in6(register_7_output), .in7(register_8_output),
    .out(ReadData2), .sel(ReadRegister2));  // open: en

  // Other names for the same wires on the sheet: clk = Clock; d[15:0] = WriteData; R1[2:0] = ReadRegister1;
  //   R2[2:0] = ReadRegister2; WE = RegisterWriteEnable
endmodule

module _1_bit_Adder (
  input  CarryIn,
  input  a,
  input  b,
  output Sum,
  output CarryOut
);

  wire and_1_out, and_2_out, xor_1_out;

  and and_1 (and_1_out, b, a);
  xor xor_1 (xor_1_out, a, b);
  or or_1 (CarryOut, and_1_out, and_2_out);
  and and_2 (and_2_out, xor_1_out, CarryIn);
  xor xor_2 (Sum, CarryIn, xor_1_out);
endmodule

module Adder (
  input  sub,
  input  [15:0] A,
  input  [15:0] B,
  output [15:0] result,
  output ovf
);

  wire n1_bit_adder_1_carryout, n1_bit_adder_2_carryout, n1_bit_adder_3_carryout, n1_bit_adder_4_carryout,
       n1_bit_adder_5_carryout, n1_bit_adder_6_carryout, n1_bit_adder_7_carryout, n1_bit_adder_8_carryout,
       n1_bit_adder_9_carryout, n1_bit_adder_10_carryout, n1_bit_adder_11_carryout, n1_bit_adder_12_carryout,
       n1_bit_adder_13_carryout, n1_bit_adder_14_carryout, n1_bit_adder_15_carryout,
       n1_bit_adder_16_carryout, xor_2_out, xor_3_out, xor_4_out, xor_5_out, xor_6_out, xor_7_out, xor_8_out,
       xor_9_out, xor_10_out, xor_11_out, xor_12_out, xor_13_out, xor_14_out, xor_15_out, xor_16_out,
       xor_17_out;

  xor xor_1 (ovf, n1_bit_adder_1_carryout, n1_bit_adder_2_carryout);
  _1_bit_Adder u_1_bit_adder_1 (
    .CarryIn(n1_bit_adder_2_carryout), .a(A[15]), .b(xor_2_out), .Sum(result[15]),
    .CarryOut(n1_bit_adder_1_carryout));
  xor xor_2 (xor_2_out, sub, B[15]);
  _1_bit_Adder u_1_bit_adder_2 (
    .CarryIn(n1_bit_adder_4_carryout), .a(A[14]), .b(xor_3_out), .Sum(result[14]),
    .CarryOut(n1_bit_adder_2_carryout));
  xor xor_3 (xor_3_out, sub, B[14]);
  _1_bit_Adder u_1_bit_adder_3 (
    .CarryIn(n1_bit_adder_5_carryout), .a(A[12]), .b(xor_5_out), .Sum(result[12]),
    .CarryOut(n1_bit_adder_3_carryout));
  _1_bit_Adder u_1_bit_adder_4 (
    .CarryIn(n1_bit_adder_3_carryout), .a(A[13]), .b(xor_4_out), .Sum(result[13]),
    .CarryOut(n1_bit_adder_4_carryout));
  xor xor_4 (xor_4_out, sub, B[13]);
  _1_bit_Adder u_1_bit_adder_5 (
    .CarryIn(n1_bit_adder_6_carryout), .a(A[11]), .b(xor_6_out), .Sum(result[11]),
    .CarryOut(n1_bit_adder_5_carryout));
  xor xor_5 (xor_5_out, sub, B[12]);
  xor xor_6 (xor_6_out, sub, B[11]);
  _1_bit_Adder u_1_bit_adder_6 (
    .CarryIn(n1_bit_adder_8_carryout), .a(A[10]), .b(xor_7_out), .Sum(result[10]),
    .CarryOut(n1_bit_adder_6_carryout));
  xor xor_7 (xor_7_out, sub, B[10]);
  _1_bit_Adder u_1_bit_adder_7 (
    .CarryIn(n1_bit_adder_9_carryout), .a(A[8]), .b(xor_10_out), .Sum(result[8]),
    .CarryOut(n1_bit_adder_7_carryout));
  _1_bit_Adder u_1_bit_adder_8 (
    .CarryIn(n1_bit_adder_7_carryout), .a(A[9]), .b(xor_8_out), .Sum(result[9]),
    .CarryOut(n1_bit_adder_8_carryout));
  xor xor_8 (xor_8_out, sub, B[9]);
  _1_bit_Adder u_1_bit_adder_9 (
    .CarryIn(n1_bit_adder_10_carryout), .a(A[7]), .b(xor_9_out), .Sum(result[7]),
    .CarryOut(n1_bit_adder_9_carryout));
  xor xor_9 (xor_9_out, sub, B[7]);
  xor xor_10 (xor_10_out, sub, B[8]);
  _1_bit_Adder u_1_bit_adder_10 (
    .CarryIn(n1_bit_adder_11_carryout), .a(A[6]), .b(xor_11_out), .Sum(result[6]),
    .CarryOut(n1_bit_adder_10_carryout));
  xor xor_11 (xor_11_out, sub, B[6]);
  _1_bit_Adder u_1_bit_adder_11 (
    .CarryIn(n1_bit_adder_12_carryout), .a(A[5]), .b(xor_12_out), .Sum(result[5]),
    .CarryOut(n1_bit_adder_11_carryout));
  _1_bit_Adder u_1_bit_adder_12 (
    .CarryIn(n1_bit_adder_13_carryout), .a(A[4]), .b(xor_14_out), .Sum(result[4]),
    .CarryOut(n1_bit_adder_12_carryout));
  xor xor_12 (xor_12_out, sub, B[5]);
  _1_bit_Adder u_1_bit_adder_13 (
    .CarryIn(n1_bit_adder_14_carryout), .a(A[3]), .b(xor_13_out), .Sum(result[3]),
    .CarryOut(n1_bit_adder_13_carryout));
  xor xor_13 (xor_13_out, sub, B[3]);
  xor xor_14 (xor_14_out, sub, B[4]);
  _1_bit_Adder u_1_bit_adder_14 (
    .CarryIn(n1_bit_adder_15_carryout), .a(A[2]), .b(xor_15_out), .Sum(result[2]),
    .CarryOut(n1_bit_adder_14_carryout));
  xor xor_15 (xor_15_out, sub, B[2]);
  _1_bit_Adder u_1_bit_adder_15 (
    .CarryIn(n1_bit_adder_16_carryout), .a(A[1]), .b(xor_16_out), .Sum(result[1]),
    .CarryOut(n1_bit_adder_15_carryout));
  _1_bit_Adder u_1_bit_adder_16 (
    .CarryIn(sub), .a(A[0]), .b(xor_17_out), .Sum(result[0]), .CarryOut(n1_bit_adder_16_carryout));
  xor xor_16 (xor_16_out, sub, B[1]);
  xor xor_17 (xor_17_out, sub, B[0]);

  // Other names for the same wires on the sheet: _0 = B[0]; _1 = B[1]; _2 = B[2]; _3 = B[3]; _4 = B[4]; _5 = B[5];
  //   _6 = B[6]; _7 = B[7]; _8 = B[8]; _9 = B[9]; _10 = B[10]; _11 = B[11]; _12 = B[12]; _13 = B[13]; _14 = B[14];
  //   _15 = B[15]
endmodule

module ALU (
  input  [2:0] ALUOp,
  input  [15:0] InputData1,
  input  [15:0] InputData2,
  input  [2:0] ShiftAmt,
  output [15:0] OutputData,
  output [1:0] Relation
);

  wire multiplexer_2_out, not_1_out, not_2_out, xor_2_out;
  wire [15:0] adder_1_result, adder_2_result, not_3_out, or_1_out, shifter_1_out_4, shifter_2_out_4,
       xor_1_out;

  not not_1 (not_1_out, 1'b0);
  not not_2 (not_2_out, 1'b0);
  Adder adder_1 (.result(adder_1_result), .sub(1'b0), .A(InputData1), .B(InputData2));  // open: ovf
  Adder adder_2 (.result(adder_2_result), .sub(not_2_out), .A(InputData1), .B(InputData2));  // open: ovf
  assign or_1_out = InputData1 | InputData2;  // OR_Gate or_1, 16 bits wide
  assign not_3_out = ~InputData1;  // NOT_Gate not_3, 16 bits wide
  assign xor_1_out = InputData1 ^ InputData2;  // XOR_Gate xor_1, 16 bits wide
  Shifter shifter_1 (.Input(InputData1), .LeftorRight(1'b0), .ShiftAmount(ShiftAmt), .out_4(shifter_1_out_4));
  Shifter shifter_2 (.Input(InputData1), .LeftorRight(not_1_out), .ShiftAmount(ShiftAmt), .out_4(shifter_2_out_4));
  Multiplexer #(.select(3), .width(16)) multiplexer_1 (
    .in0(adder_1_result), .in1(adder_2_result), .in2(or_1_out), .in3(not_3_out), .in4(xor_1_out),
    .in5(shifter_1_out_4), .in6(shifter_2_out_4), .out(OutputData), .sel(ALUOp));  // open: in7, en
  xor xor_2 (xor_2_out, InputData1[15], InputData2[15]);
  // Probe on xor_1_out
  // Probe on adder_2_result
  Multiplexer #(.enable("false")) multiplexer_2 (
    .in0(xor_2_out), .in1(InputData1[15]), .out(multiplexer_2_out), .sel(xor_2_out));
  nor nor_1 (Relation[1], xor_1_out[0], xor_1_out[1], xor_1_out[2], xor_1_out[3], xor_1_out[4], xor_1_out[5], xor_1_out[6], xor_1_out[7], xor_1_out[9], xor_1_out[10], xor_1_out[11], xor_1_out[12], xor_1_out[13], xor_1_out[14], xor_1_out[15], xor_1_out[8]);
  Multiplexer #(.enable("false")) multiplexer_3 (
    .in0(adder_2_result[15]), .in1(multiplexer_2_out), .out(Relation[0]), .sel(xor_2_out));

  // Other names for the same wires on the sheet: OT[2:0] = ALUOp

  // Notes on the sheet:
  //   000: Add, 001: Sub, 010: Or, 011: Not, 100: Xor, 101: RShifter, 110: LShifter
  //   branch equal
  //   0: different, 1: same
  //   0: 1>2, 1: 1<2
  //   00: 1>2       01: 1<2       10: 1=2
  //   branch less than
endmodule

module _1_bit_Shifter (
  input  [15:0] in_1,
  output [15:0] out_2,
  output [15:0] out_3
);


  assign out_2 = {{2{in_1[15]}}, in_1[14:1]};
  assign out_3 = {in_1[14:0], 1'b0};

  // Notes on the sheet:
  //   1-bit right shift:
  //   1-bit left shift:
endmodule

module Shifter (
  input  [15:0] Input,
  input  LeftorRight,
  input  [2:0] ShiftAmount,
  output [15:0] out_4
);

  wire [15:0] n1_bit_shifter_1_out_2, n1_bit_shifter_1_out_3, n1_bit_shifter_2_out_2, n1_bit_shifter_2_out_3,
       n1_bit_shifter_3_out_2, n1_bit_shifter_3_out_3, n1_bit_shifter_4_out_2, n1_bit_shifter_4_out_3,
       n1_bit_shifter_5_out_2, n1_bit_shifter_5_out_3, n1_bit_shifter_6_out_2, n1_bit_shifter_6_out_3,
       n1_bit_shifter_7_out_2, n1_bit_shifter_7_out_3, Shift1, Shift2, Shift3, Shift4, Shift5, Shift6, Shift7;

  _1_bit_Shifter u_1_bit_shifter_1 (.in_1(Input), .out_2(n1_bit_shifter_1_out_2), .out_3(n1_bit_shifter_1_out_3));
  Multiplexer #(.width(16)) multiplexer_1 (
    .in0(n1_bit_shifter_1_out_2), .in1(n1_bit_shifter_1_out_3), .out(Shift1), .sel(LeftorRight));  // open: en
  // Probe on Shift1
  Multiplexer #(.select(3), .width(16)) multiplexer_2 (
    .in0(Input), .in1(Shift1), .in2(Shift2), .in3(Shift3), .in4(Shift4), .in5(Shift5), .in6(Shift6),
    .in7(Shift7), .out(out_4), .sel(ShiftAmount));  // open: en
  _1_bit_Shifter u_1_bit_shifter_2 (.in_1(Shift1), .out_2(n1_bit_shifter_2_out_2), .out_3(n1_bit_shifter_2_out_3));
  Multiplexer #(.width(16)) multiplexer_3 (
    .in0(n1_bit_shifter_2_out_2), .in1(n1_bit_shifter_2_out_3), .out(Shift2), .sel(LeftorRight));  // open: en
  // Probe on Shift2
  _1_bit_Shifter u_1_bit_shifter_3 (.in_1(Shift2), .out_2(n1_bit_shifter_3_out_2), .out_3(n1_bit_shifter_3_out_3));
  Multiplexer #(.width(16)) multiplexer_4 (
    .in0(n1_bit_shifter_3_out_2), .in1(n1_bit_shifter_3_out_3), .out(Shift3), .sel(LeftorRight));  // open: en
  _1_bit_Shifter u_1_bit_shifter_4 (.in_1(Shift3), .out_2(n1_bit_shifter_4_out_2), .out_3(n1_bit_shifter_4_out_3));
  // Probe on Shift3
  Multiplexer #(.width(16)) multiplexer_5 (
    .in0(n1_bit_shifter_4_out_2), .in1(n1_bit_shifter_4_out_3), .out(Shift4), .sel(LeftorRight));  // open: en
  // Probe on Shift4
  _1_bit_Shifter u_1_bit_shifter_5 (.in_1(Shift4), .out_2(n1_bit_shifter_5_out_2), .out_3(n1_bit_shifter_5_out_3));
  Multiplexer #(.width(16)) multiplexer_6 (
    .in0(n1_bit_shifter_5_out_2), .in1(n1_bit_shifter_5_out_3), .out(Shift5), .sel(LeftorRight));  // open: en
  // Probe on Shift5
  _1_bit_Shifter u_1_bit_shifter_6 (.in_1(Shift5), .out_2(n1_bit_shifter_6_out_2), .out_3(n1_bit_shifter_6_out_3));
  Multiplexer #(.width(16)) multiplexer_7 (
    .in0(n1_bit_shifter_6_out_2), .in1(n1_bit_shifter_6_out_3), .out(Shift6), .sel(LeftorRight));  // open: en
  // Probe on Shift6
  _1_bit_Shifter u_1_bit_shifter_7 (.in_1(Shift6), .out_2(n1_bit_shifter_7_out_2), .out_3(n1_bit_shifter_7_out_3));
  Multiplexer #(.width(16)) multiplexer_8 (
    .in0(n1_bit_shifter_7_out_2), .in1(n1_bit_shifter_7_out_3), .out(Shift7), .sel(LeftorRight));  // open: en
  // Probe on Shift7

  // Other names for the same wires on the sheet: LR = LeftorRight; Shift0[15:0] = Input

  // Notes on the sheet:
  //   0: RIght, 1: Left
endmodule

module SignExtender (
  input  [5:0] in_1,
  output [15:0] out_2
);


  assign out_2 = {{11{in_1[5]}}, in_1[4:0]};
endmodule

module InstructionDecoder (
  input  [15:0] ManualInstruction,
  output [2:0] Rs,
  output [2:0] Rt,
  output [2:0] Rd,
  output [2:0] ShAmt,
  output [5:0] Imm,
  output [11:0] Addr,
  output RegWriteEnable,
  output RAMWriteEnable,
  output MUX_RtData_Imm,
  output MUX_Rd_Rt,
  output MUX_ALU_Result_Memory,
  output [2:0] ALUOpType,
  output [1:0] MUX_0_beq_blt,
  output [1:0] MUX_0_j_jr,
  output MUX_0_jal,
  output TTYWriteEnable,
  output KeyboardRE
);

  wire [2:0] undriven, undriven_2, undriven_3, undriven_4, undriven_5, undriven_6, undriven_7;

  // Probe on ManualInstruction[11:0]
  Multiplexer #(.select(4), .enable("false")) multiplexer_1 (
    .in0(1'b1), .in1(1'b0), .in2(1'b0), .in3(1'b0), .in4(1'b1), .in5(1'b1), .in6(1'b1), .in7(1'b1),
    .in8(1'b1), .in9(1'b1), .in10(1'b1), .in11(1'b0), .in12(1'b1), .in13(1'b0), .in14(1'b0), .in15(1'b1),
    .out(RegWriteEnable), .sel(ManualInstruction[15:12]));
  Multiplexer #(.select(4), .enable("false")) multiplexer_2 (
    .in0(1'b1), .in1(1'b1), .in2(1'b0), .in3(1'b0), .in4(1'b0), .in5(1'b0), .in6(1'b1), .in7(1'b0),
    .in8(1'b0), .in9(1'b0), .in10(1'b0), .in11(1'b0), .in12(1'b0), .in13(1'b0), .in14(1'b0), .in15(1'b0),
    .out(MUX_RtData_Imm), .sel(ManualInstruction[15:12]));
  Multiplexer #(.select(4), .width(3), .enable("false")) multiplexer_3 (
    .in0(3'b000), .in1(3'b000), .in2(undriven_5), .in3(undriven), .in4(3'b011), .in5(3'b100), .in6(3'b000),
    .in7(3'b000), .in8(3'b001), .in9(3'b101), .in10(3'b110), .in11(undriven_2), .in12(undriven_6),
    .in13(undriven_3), .in14(undriven_7), .in15(undriven_4), .out(ALUOpType), .sel(ManualInstruction[15:12]));
  Multiplexer #(.select(4), .enable("false")) multiplexer_4 (
    .in0(1'b0), .in1(1'b0), .in2(1'b0), .in3(1'b0), .in4(1'b0), .in5(1'b0), .in6(1'b0), .in7(1'b0),
    .in8(1'b0), .in9(1'b0), .in10(1'b0), .in11(1'b0), .in12(1'b0), .in13(1'b0), .in14(1'b1), .in15(1'b0),
    .out(TTYWriteEnable), .sel(ManualInstruction[15:12]));
  // Probe on ManualInstruction[15:12]
  // Probe on ManualInstruction[11:0]
  Multiplexer #(.select(4), .enable("false")) multiplexer_5 (
    .in0(1'b0), .in1(1'b1), .in2(1'b0), .in3(1'b0), .in4(1'b0), .in5(1'b0), .in6(1'b0), .in7(1'b0),
    .in8(1'b0), .in9(1'b0), .in10(1'b0), .in11(1'b0), .in12(1'b0), .in13(1'b0), .in14(1'b0), .in15(1'b0),
    .out(RAMWriteEnable), .sel(ManualInstruction[15:12]));
  Multiplexer #(.select(4), .enable("false")) multiplexer_6 (
    .in0(1'b1), .in1(1'b0), .in2(1'b0), .in3(1'b0), .in4(1'b0), .in5(1'b0), .in6(1'b1), .in7(1'b0),
    .in8(1'b0), .in9(1'b0), .in10(1'b0), .in11(1'b0), .in12(1'b0), .in13(1'b0), .in14(1'b0), .in15(1'b0),
    .out(MUX_Rd_Rt), .sel(ManualInstruction[15:12]));
  Multiplexer #(.select(4), .width(2), .enable("false")) multiplexer_7 (
    .in0(2'b00), .in1(2'b00), .in2(2'b01), .in3(2'b10), .in4(2'b00), .in5(2'b00), .in6(2'b00), .in7(2'b00),
    .in8(2'b00), .in9(2'b00), .in10(2'b00), .in11(2'b00), .in12(2'b00), .in13(2'b00), .in14(2'b00),
    .in15(2'b00), .out(MUX_0_beq_blt), .sel(ManualInstruction[15:12]));
  Multiplexer #(.select(4), .enable("false")) multiplexer_8 (
    .in0(1'b0), .in1(1'b0), .in2(1'b0), .in3(1'b0), .in4(1'b0), .in5(1'b0), .in6(1'b0), .in7(1'b0),
    .in8(1'b0), .in9(1'b0), .in10(1'b0), .in11(1'b0), .in12(1'b0), .in13(1'b0), .in14(1'b0), .in15(1'b1),
    .out(KeyboardRE), .sel(ManualInstruction[15:12]));
  Multiplexer #(.select(4), .enable("false")) multiplexer_9 (
    .in0(1'b1), .in1(1'b0), .in2(1'b0), .in3(1'b0), .in4(1'b0), .in5(1'b0), .in6(1'b0), .in7(1'b0),
    .in8(1'b0), .in9(1'b0), .in10(1'b0), .in11(1'b0), .in12(1'b0), .in13(1'b0), .in14(1'b0), .in15(1'b0),
    .out(MUX_ALU_Result_Memory), .sel(ManualInstruction[15:12]));
  Multiplexer #(.select(4), .width(2), .enable("false")) multiplexer_10 (
    .in0(2'b00), .in1(2'b00), .in2(2'b00), .in3(2'b00), .in4(2'b00), .in5(2'b00), .in6(2'b00), .in7(2'b00),
    .in8(2'b00), .in9(2'b00), .in10(2'b00), .in11(2'b01), .in12(2'b01), .in13(2'b10), .in14(2'b00),
    .in15(2'b00), .out(MUX_0_j_jr), .sel(ManualInstruction[15:12]));
  Multiplexer #(.select(4), .enable("false")) multiplexer_11 (
    .in0(1'b0), .in1(1'b0), .in2(1'b0), .in3(1'b0), .in4(1'b0), .in5(1'b0), .in6(1'b0), .in7(1'b0),
    .in8(1'b0), .in9(1'b0), .in10(1'b0), .in11(1'b0), .in12(1'b1), .in13(1'b0), .in14(1'b0), .in15(1'b0),
    .out(MUX_0_jal), .sel(ManualInstruction[15:12]));

  assign Addr = ManualInstruction[11:0];
  assign Imm = ManualInstruction[5:0];
  assign Rd = ManualInstruction[5:3];
  assign Rs = ManualInstruction[11:9];
  assign Rt = ManualInstruction[8:6];
  assign ShAmt = ManualInstruction[2:0];

  // Other names for the same wires on the sheet: Else[11:0] = ManualInstruction[11:0];
  //   OpCode[3:0] = ManualInstruction[15:12]

  // Notes on the sheet:
  //   lw
  //   sw
  //   beq
  //   blt
  //   not
  //   xor
  //   addi
  //   add
  //   sub
  //   shra
  //   shl
  //   j
  //   jal
  //   jr
  //   output
  //   input
  //   lw
  //   sw
  //   beq
  //   blt
  //   not
  //   xor
  //   addi
  //   add
  //   sub
  //   shra
  //   shl
  //   j
  //   jal
  //   jr
  //   output
  //   input
  //   lw
  //   sw
  //   beq
  //   blt
  //   not
  //   xor
  //   addi
  //   add
  //   sub
  //   shra
  //   shl
  //   j
  //   jal
  //   jr
  //   output
  //   input
  //   lw
  //   sw
  //   beq
  //   blt
  //   not
  //   xor
  //   addi
  //   add
  //   sub
  //   shra
  //   shl
  //   j
  //   jal
  //   jr
  //   output
  //   input
  //   output, input
  //   beq, blt, j, jal, jr, output, input
  //   lw
  //   sw
  //   beq
  //   blt
  //   not
  //   xor
  //   addi
  //   add
  //   sub
  //   shra
  //   shl
  //   j
  //   jal
  //   jr
  //   output
  //   input
  //   lw
  //   sw
  //   beq
  //   blt
  //   not
  //   xor
  //   addi
  //   add
  //   sub
  //   shra
  //   shl
  //   j
  //   jal
  //   jr
  //   output
  //   input
  //   lw
  //   sw
  //   beq
  //   blt
  //   not
  //   xor
  //   addi
  //   add
  //   sub
  //   shra
  //   shl
  //   j
  //   jal
  //   jr
  //   output
  //   input
  //   lw
  //   sw
  //   beq
  //   blt
  //   not
  //   xor
  //   addi
  //   add
  //   sub
  //   shra
  //   shl
  //   j
  //   jal
  //   jr
  //   output
  //   input
  //   sw, beq, blt, j, jal, jr, output
  //   lw
  //   sw
  //   beq
  //   blt
  //   not
  //   xor
  //   addi
  //   add
  //   sub
  //   shra
  //   shl
  //   jal
  //   jr
  //   output
  //   input
  //   lw
  //   sw
  //   beq
  //   blt
  //   not
  //   xor
  //   addi
  //   add
  //   sub
  //   shra
  //   shl
  //   jal
  //   jr
  //   output
  //   input
  //   j
  //   j
  //   sw, beq, blt, j, jal, jr, output, input
  //   lw
  //   sw
  //   beq
  //   blt
  //   not
  //   xor
  //   addi
  //   add
  //   sub
  //   shra
  //   shl
  //   j
  //   jal
  //   jr
  //   output
  //   input
endmodule

module ProgramCounter (
  input  Clock,
  input  reset,
  input  [15:0] Input,
  output [15:0] Output
);

  D_Flip_Flop d_ff_1 (.clk(Clock), .D(Input[0]), .Q(Output[0]), .en(1'b1), .reset(reset));  // open: Qn, preset
  D_Flip_Flop d_ff_2 (.clk(Clock), .D(Input[1]), .Q(Output[1]), .en(1'b1), .reset(reset));  // open: Qn, preset
  D_Flip_Flop d_ff_3 (.clk(Clock), .D(Input[2]), .Q(Output[2]), .en(1'b1), .reset(reset));  // open: Qn, preset
  D_Flip_Flop d_ff_4 (.clk(Clock), .D(Input[3]), .Q(Output[3]), .en(1'b1), .reset(reset));  // open: Qn, preset
  D_Flip_Flop d_ff_5 (.clk(Clock), .D(Input[4]), .Q(Output[4]), .en(1'b1), .reset(reset));  // open: Qn, preset
  D_Flip_Flop d_ff_6 (.clk(Clock), .D(Input[5]), .Q(Output[5]), .en(1'b1), .reset(reset));  // open: Qn, preset
  D_Flip_Flop d_ff_7 (.clk(Clock), .D(Input[6]), .Q(Output[6]), .en(1'b1), .reset(reset));  // open: Qn, preset
  D_Flip_Flop d_ff_8 (.clk(Clock), .D(Input[7]), .Q(Output[7]), .en(1'b1), .reset(reset));  // open: Qn, preset
  D_Flip_Flop d_ff_9 (.clk(Clock), .D(Input[8]), .Q(Output[8]), .en(1'b1), .reset(reset));  // open: Qn, preset
  D_Flip_Flop d_ff_10 (.clk(Clock), .D(Input[9]), .Q(Output[9]), .en(1'b1), .reset(reset));  // open: Qn, preset
  D_Flip_Flop d_ff_11 (.clk(Clock), .D(Input[10]), .Q(Output[10]), .en(1'b1), .reset(reset));  // open: Qn, preset
  D_Flip_Flop d_ff_12 (.clk(Clock), .D(Input[11]), .Q(Output[11]), .en(1'b1), .reset(reset));  // open: Qn, preset
  D_Flip_Flop d_ff_13 (.clk(Clock), .D(Input[12]), .Q(Output[12]), .en(1'b1), .reset(reset));  // open: Qn, preset
  D_Flip_Flop d_ff_14 (.clk(Clock), .D(Input[13]), .Q(Output[13]), .en(1'b1), .reset(reset));  // open: Qn, preset
  D_Flip_Flop d_ff_15 (.clk(Clock), .D(Input[14]), .Q(Output[14]), .en(1'b1), .reset(reset));  // open: Qn, preset
  D_Flip_Flop d_ff_16 (.clk(Clock), .D(Input[15]), .Q(Output[15]), .en(1'b1), .reset(reset));  // open: Qn, preset

  // Other names for the same wires on the sheet: clk = Clock
endmodule
